// Logisim project Senior's-ckt.circ as structural Verilog: 7 circuits, main circuit main
module main (
  input  [15:0] in_1,
  input  [15:0] in_2,
  output out_3,
  output [10:0] out_4,
  output [3:0] out_5
);

  wire big_alu_1_out_6, exponent_fraction_1_out_13, exponent_fraction_1_out_14, rounding_1_out_5,
       small_alu_1_out_4;
  wire [3:0] exponent_fraction_1_out_12, rounding_1_out_6, small_alu_1_out_3;
  wire [11:0] big_alu_1_out_5, exponent_fraction_1_out_10, exponent_fraction_1_out_11, rounding_1_out_4,
       shifting_1_out_3;

  SMALL_ALU small_alu_1 (.in_1(in_1[14:11]), .in_2(in_2[14:11]), .out_4(small_alu_1_out_4), .out_3(small_alu_1_out_3));
  Rounding rounding_1 (
    .carry_input(big_alu_1_out_6), .in_2(big_alu_1_out_5), .in_3(exponent_fraction_1_out_12),
    .out_4(rounding_1_out_4), .out_5(rounding_1_out_5), .out_6(rounding_1_out_6));
  Exponent_Fraction exponent_fraction_1 (
    .in_1(in_1[10:0]), .in_2(in_2[10:0]), .in_3(in_1[14:11]), .in_4(in_2[14:11]), .in_5(small_alu_1_out_4),
    .in_6(small_alu_1_out_4), .in_7(small_alu_1_out_4), .out_10(exponent_fraction_1_out_10),
    .out_11(exponent_fraction_1_out_11), .out_12(exponent_fraction_1_out_12), .in_8(in_1[15]),
    .sign_B(in_2[15]), .out_13(exponent_fraction_1_out_13), .out_14(exponent_fraction_1_out_14));
  Shifting shifting_1 (.in_1(exponent_fraction_1_out_11), .in_2(small_alu_1_out_3), .out_3(shifting_1_out_3));
  Normalization normalization_1 (
    .fraction(rounding_1_out_4), .exponent(rounding_1_out_6), .carry(rounding_1_out_5), .out_4(out_4),
    .out_5(out_5));
  BIG_ALU big_alu_1 (
    .in_1(exponent_fraction_1_out_10), .in_2(shifting_1_out_3), .sign_1(exponent_fraction_1_out_13),
    .sign_2(exponent_fraction_1_out_14), .out_5(big_alu_1_out_5), .output_sign_bit(out_3),
    .out_6(big_alu_1_out_6));

  // Notes on the sheet:
  //   A(0)
  //   B(1)
  //   sign bit
  //   rounding
  //   exponent and fraction
  //   absolute diff
  //   normalization
  //   S1
  //   s2
  //   basically just a shifter
  //   Shifting
endmodule

module SMALL_ALU (
  input  [3:0] in_1,
  input  [3:0] in_2,
  output [3:0] out_3,
  output out_4
);

  wire [3:0] negator_1_out, subtractor_1_out;

  Subtractor #(.width(4)) subtractor_1 (.a(in_1), .b(in_2), .out(subtractor_1_out), .bout(out_4));  // open: bin
  Negator #(.width(4)) negator_1 (.in(subtractor_1_out), .out(negator_1_out));
  Multiplexer #(.width(4)) multiplexer_1 (
    .in0(subtractor_1_out), .in1(negator_1_out), .out(out_3), .sel(out_4));  // open: en
endmodule

module Exponent_Fraction (
  input  [10:0] in_1,
  input  [10:0] in_2,
  input  [3:0] in_3,
  input  [3:0] in_4,
  input  in_5,
  input  in_6,
  input  in_7,
  input  in_8,
  input  sign_B,
  output [11:0] out_10,
  output [11:0] out_11,
  output [3:0] out_12,
  output out_13,
  output out_14
);

  wire not_1_out;
  wire [11:0] bit_extender_1_out, bit_extender_2_out;

  assign bit_extender_1_out = {{1{1'b1}}, in_1};  // Bit_Extender bit_extender_1
  assign bit_extender_2_out = {{1{1'b1}}, in_2};  // Bit_Extender bit_extender_2
  not not_1 (not_1_out, in_6);
  Multiplexer #(.width(12)) multiplexer_1 (
    .in0(bit_extender_1_out), .in1(bit_extender_2_out), .out(out_10), .sel(in_5));  // open: en
  Multiplexer #(.width(12)) multiplexer_2 (
    .in0(bit_extender_1_out), .in1(bit_extender_2_out), .out(out_11), .sel(not_1_out));  // open: en
  Multiplexer #(.width(4)) multiplexer_3 (.in0(in_3), .in1(in_4), .out(out_12), .sel(in_7));  // open: en
  Multiplexer multiplexer_4 (.in0(in_8), .in1(sign_B), .out(out_13), .sel(in_5));  // open: en
  Multiplexer multiplexer_5 (.in0(in_8), .in1(sign_B), .out(out_14), .sel(not_1_out));  // open: en

  // Notes on the sheet:
  //   sign A
  //   sign bit of small alu output x 3
  //   exponent
endmodule

module BIG_ALU (
  input  [11:0] in_1,
  input  [11:0] in_2,
  input  sign_1,
  input  sign_2,
  output [11:0] out_5,
  output out_6,
  output output_sign_bit
);

  wire adder_1_cout, comparator_1_gt, subtractor_1_bout, xor_1_out;
  wire [11:0] adder_1_out, multiplexer_1_out, negator_1_out, subtractor_1_out;

  Adder #(.width(12)) adder_1 (.a(in_1), .b(in_2), .out(adder_1_out), .cout(adder_1_cout));  // open: cin
  Subtractor #(.width(12)) subtractor_1 (
    .a(in_1), .b(in_2), .out(subtractor_1_out), .bout(subtractor_1_bout));  // open: bin
  xor xor_1 (xor_1_out, sign_1, sign_2);
  Negator #(.width(12)) negator_1 (.in(subtractor_1_out), .out(negator_1_out));
  Multiplexer #(.width(12)) multiplexer_1 (
    .in0(subtractor_1_out), .in1(negator_1_out), .out(multiplexer_1_out), .sel(subtractor_1_bout));  // open: en
  Comparator #(.width(12), .mode("unsigned")) comparator_1 (.a(in_1), .b(in_2), .gt(comparator_1_gt));  // open: eq, lt
  Multiplexer #(.width(12)) multiplexer_2 (
    .in0(adder_1_out), .in1(multiplexer_1_out), .out(out_5), .sel(xor_1_out));  // open: en
  Multiplexer multiplexer_3 (.in0(sign_2), .in1(sign_1), .out(output_sign_bit), .sel(comparator_1_gt));  // open: en
  Multiplexer multiplexer_4 (.in0(adder_1_cout), .in1(subtractor_1_bout), .out(out_6), .sel(xor_1_out));  // open: en

  // Notes on the sheet:
  //   here, they didnt consider sign bit output then 2 signs are same
  //   carry from this alu
endmodule

module Shifting (
  input  [11:0] in_1,
  input  [3:0] in_2,
  output [11:0] out_3
);

  wire comparator_1_eq;
  wire [11:0] shifter_1_out;

  Comparator #(.width(4), .mode("unsigned")) comparator_1 (
    .a(in_2), .b(4'b0000), .eq(comparator_1_eq));  // open: gt, lt
  Shifter #(.width(12), .shift("lr")) shifter_1 (.in(in_1), .\dist (in_2), .out(shifter_1_out));
  Multiplexer #(.width(12)) multiplexer_1 (
    .in0(shifter_1_out), .in1(in_1), .out(out_3), .sel(comparator_1_eq));  // open: en
endmodule

module Normalization (
  input  [11:0] fraction,
  input  [3:0] exponent,
  input  carry,
  output [10:0] out_4,
  output [3:0] out_5
);

  wire comparator_1_eq, or_1_out;
  wire [3:0] adder_1_out, bit_extender_1_out, bitfinder_1_index, subtractor_1_out, subtractor_2_out;
  wire [10:0] shifter_2_out;
  wire [11:0] shifter_1_out;

  assign bit_extender_1_out = {{3{1'b0}}, carry};  // Bit_Extender bit_extender_1
  Shifter #(.width(12), .shift("lr")) shifter_1 (.in(fraction), .\dist (bit_extender_1_out), .out(shifter_1_out));
  Adder #(.width(4)) adder_1 (.a(exponent), .b(bit_extender_1_out), .out(adder_1_out));  // open: cin, cout
  or or_1 (or_1_out, shifter_1_out[11], carry);
  Comparator #(.width(1)) comparator_1 (.a(1'b0), .b(or_1_out), .eq(comparator_1_eq));  // open: gt, lt
  BitFinder #(.width(11), .\type ("high1")) bitfinder_1 (
    .in(shifter_1_out[10:0]), .index(bitfinder_1_index));  // open: found
  Subtractor #(.width(4)) subtractor_1 (.a(4'b1011), .b(bitfinder_1_index), .out(subtractor_1_out));  // open: bin, bout
  Subtractor #(.width(4)) subtractor_2 (
    .a(adder_1_out), .b(subtractor_1_out), .out(subtractor_2_out));  // open: bin, bout
  Shifter #(.width(11)) shifter_2 (.in(shifter_1_out[10:0]), .\dist (subtractor_1_out), .out(shifter_2_out));
  Multiplexer #(.width(11)) multiplexer_1 (
    .in0(shifter_1_out[10:0]), .in1(shifter_2_out), .out(out_4), .sel(comparator_1_eq));  // open: en
  Multiplexer #(.width(4)) multiplexer_2 (
    .in0(adder_1_out), .in1(subtractor_2_out), .out(out_5), .sel(comparator_1_eq));  // open: en

  // Notes on the sheet:
  //   Right Shift
  //   left shift means exponent decreases
endmodule

module Rounding (
  input  carry_input,
  input  [11:0] in_2,
  input  [3:0] in_3,
  output [11:0] out_4,
  output out_5,
  output [3:0] out_6
);

  wire adder_2_cout, bitselector_1_out;
  wire [3:0] bit_extender_3_out;
  wire [12:0] adder_1_out, adder_2_out, bit_extender_1_out, bit_extender_2_out, shifter_1_out;

  assign bit_extender_1_out = {{12{1'b0}}, carry_input};  // Bit_Extender bit_extender_1
  assign bit_extender_2_out = {{1{1'b0}}, in_2};  // Bit_Extender bit_extender_2
  Shifter #(.width(13)) shifter_1 (.in(bit_extender_1_out), .\dist (4'b1100), .out(shifter_1_out));
  Adder #(.width(13)) adder_1 (.a(shifter_1_out), .b(bit_extender_2_out), .out(adder_1_out));  // open: cin, cout
  BitSelector #(.width(13)) bitselector_1 (.in(adder_1_out), .out(bitselector_1_out), .sel(4'b0010));
  Adder #(.width(13)) adder_2 (.a(adder_1_out), .b(13'h1), .out(adder_2_out), .cout(adder_2_cout));  // open: cin
  assign bit_extender_3_out = {{3{1'b0}}, adder_2_cout};  // Bit_Extender bit_extender_3
  Multiplexer #(.width(13)) multiplexer_1 (
    .in0(adder_1_out), .in1(adder_2_out), .out({out_5, out_4}), .sel(bitselector_1_out));  // open: en
  Adder #(.width(4)) adder_3 (.a(in_3), .b(bit_extender_3_out), .out(out_6));  // open: cin, cout

  // Notes on the sheet:
  //   fraction input
  //   exponent input
endmodule
