// Logisim project myCirc.circ as structural Verilog: 4 circuits, main circuit main
module main (
  input  [15:0] B,
  input  [15:0] A,
  output [10:0] out_3,
  output [3:0] out_4,
  output sign
);

  wire and_1_out, calculates_absolute_exponent_diff_b___a,
       calculates_sum__returns_appropriate_sign_and_carry_carry_out, comparator_1_eq, comparator_2_eq,
       multiplexer_4_out, multiplexer_5_out, normalize_1_exponent_out_of_range, or_1_out;
  wire [3:0] calculates_absolute_exponent_diff_out_3, multiplexer_1_out, normalize_1_out_5;
  wire [11:0] bit_extender_1_out, bit_extender_2_out,
       calculates_sum__returns_appropriate_sign_and_carry_output, multiplexer_2_out, multiplexer_3_out,
       shifter_1_out;

  small_ALU calculates_absolute_exponent_diff (
    .A_s_exponent(A[14:11]), .B_s_exponent(B[14:11]), .out_3(calculates_absolute_exponent_diff_out_3),
    .B___A(calculates_absolute_exponent_diff_b___a));
  Multiplexer #(.width(4), .enable("false")) multiplexer_1 (
    .in0(A[14:11]), .in1(B[14:11]), .out(multiplexer_1_out), .sel(calculates_absolute_exponent_diff_b___a));
  assign bit_extender_1_out = {{1{1'b1}}, A[10:0]};  // Bit_Extender bit_extender_1
  Comparator #(.width(4)) comparator_1 (
    .a(calculates_absolute_exponent_diff_out_3), .b(4'b0000), .eq(comparator_1_eq));  // open: gt, lt
  Comparator #(.width(12)) comparator_2 (
    .a(calculates_sum__returns_appropriate_sign_and_carry_output), .b({12{1'b0}}), .eq(comparator_2_eq));  // open: gt, lt
  Multiplexer #(.width(12), .enable("false")) multiplexer_2 (
    .in0(bit_extender_2_out), .in1(bit_extender_1_out), .out(multiplexer_2_out),
    .sel(calculates_absolute_exponent_diff_b___a));
  Multiplexer #(.width(12), .enable("false")) multiplexer_3 (
    .in0(bit_extender_1_out), .in1(bit_extender_2_out), .out(multiplexer_3_out),
    .sel(calculates_absolute_exponent_diff_b___a));
  Shifter #(.width(12), .shift("lr")) shifter_1 (
    .in(multiplexer_2_out), .\dist (calculates_absolute_exponent_diff_out_3), .out(shifter_1_out));
  Normalize normalize_1 (
    .fraction(calculates_sum__returns_appropriate_sign_and_carry_output), .exponent(multiplexer_1_out),
    .carry(calculates_sum__returns_appropriate_sign_and_carry_carry_out), .out_4(out_3),
    .out_5(normalize_1_out_5), .Exponent_out_of_range(normalize_1_exponent_out_of_range));
  Multiplexer #(.enable("false")) multiplexer_4 (
    .in0(A[15]), .in1(B[15]), .out(multiplexer_4_out), .sel(calculates_absolute_exponent_diff_b___a));
  and and_1 (and_1_out, comparator_2_eq, comparator_1_eq, or_1_out);
  Multiplexer #(.enable("false")) multiplexer_5 (
    .in0(B[15]), .in1(A[15]), .out(multiplexer_5_out), .sel(calculates_absolute_exponent_diff_b___a));
  Multiplexer #(.width(4), .enable("false")) multiplexer_6 (
    .in0(normalize_1_out_5), .in1(4'b0000), .out(out_4), .sel(and_1_out));
  assign bit_extender_2_out = {{1{1'b1}}, B[10:0]};  // Bit_Extender bit_extender_2
  big_ALU calculates_sum__returns_appropriate_sign_and_carry (
    .A(shifter_1_out), .B(multiplexer_3_out), .sign_A(multiplexer_5_out), .sign_B(multiplexer_4_out),
    .\output (calculates_sum__returns_appropriate_sign_and_carry_output),
    .carry_out(calculates_sum__returns_appropriate_sign_and_carry_carry_out), .sign_bit_output(sign));
  or or_1 (or_1_out, A[15], B[15]);

  // Notes on the sheet:
  //   0 has A's E
  //   0 has B, 1 has A
  //   0 has A, 1 has B
  //   fraction with smaller exponent
endmodule

module small_ALU (
  input  [3:0] A_s_exponent,
  input  [3:0] B_s_exponent,
  output [3:0] out_3,
  output B___A
);

  wire [3:0] negator_1_out, subtractor_1_out;

  Subtractor #(.width(4)) subtractor_1 (
    .a(A_s_exponent), .b(B_s_exponent), .out(subtractor_1_out), .bout(B___A));  // open: bin
  Negator #(.width(4)) negator_1 (.in(subtractor_1_out), .out(negator_1_out));
  Multiplexer #(.width(4), .enable("false")) multiplexer_1 (
    .in0(subtractor_1_out), .in1(negator_1_out), .out(out_3), .sel(B___A));

  // Notes on the sheet:
  //   sign bit
  //   absolute exponent difference
endmodule

module Normalize (
  input  [11:0] fraction,
  input  [3:0] exponent,
  input  carry,
  output [10:0] out_4,
  output [3:0] out_5,
  output Exponent_out_of_range
);

  wire adder_1_cout, adder_3_cout, and_1_out, and_2_out, bitfinder_1_found, subtractor_2_bout;
  wire [3:0] adder_1_out, bit_extender_1_out, bit_extender_3_out, bitfinder_1_index, multiplexer_1_out,
       subtractor_1_out;
  wire [11:0] adder_2_out, adder_3_out, adder_4_out, bit_extender_2_out, bit_extender_4_out, shifter_1_out,
       shifter_2_out, shifter_3_out, shifter_5_out;
  wire [11:11] shifter_4_out;

  assign bit_extender_1_out = {{3{1'b0}}, carry};  // Bit_Extender bit_extender_1
  Shifter #(.width(12), .shift("lr")) shifter_1 (.in(fraction), .\dist (bit_extender_1_out), .out(shifter_1_out));
  assign bit_extender_2_out = {{11{1'b0}}, carry};  // Bit_Extender bit_extender_2
  Adder #(.width(4)) adder_1 (
    .a(exponent), .b(bit_extender_1_out), .out(adder_1_out), .cin(adder_3_cout), .cout(adder_1_cout));
  and and_1 (and_1_out, fraction[0], carry);
  Shifter #(.width(12)) shifter_2 (.in(bit_extender_2_out), .\dist (4'b1011), .out(shifter_2_out));
  Adder #(.width(12)) adder_2 (.a(shifter_1_out), .b(shifter_2_out), .out(adder_2_out));  // open: cin, cout
  Adder #(.width(12)) adder_3 (
    .a(adder_2_out), .b({12{1'b0}}), .out(adder_3_out), .cin(and_1_out), .cout(adder_3_cout));
  assign bit_extender_3_out = {{3{1'b0}}, adder_3_cout};  // Bit_Extender bit_extender_3
  BitFinder #(.width(12), .\type ("high1")) bitfinder_1 (
    .in(adder_4_out), .index(bitfinder_1_index), .found(bitfinder_1_found));
  Subtractor #(.width(4)) subtractor_1 (.a(4'b1011), .b(bitfinder_1_index), .out(subtractor_1_out));  // open: bin, bout
  and and_2 (and_2_out, adder_3_out[0], adder_3_cout);
  Shifter #(.width(12), .shift("lr")) shifter_3 (.in(adder_3_out), .\dist (bit_extender_3_out), .out(shifter_3_out));
  assign bit_extender_4_out = {{11{1'b0}}, adder_3_cout};  // Bit_Extender bit_extender_4
  Shifter #(.width(12)) shifter_4 (.in(adder_4_out), .\dist (subtractor_1_out), .out({shifter_4_out[11], out_4}));
  Multiplexer #(.width(4), .enable("false")) multiplexer_1 (
    .in0(4'b0000), .in1(subtractor_1_out), .out(multiplexer_1_out), .sel(bitfinder_1_found));
  Subtractor #(.width(4)) subtractor_2 (
    .a(adder_1_out), .b(multiplexer_1_out), .out(out_5), .bout(subtractor_2_bout));  // open: bin
  Shifter #(.width(12)) shifter_5 (.in(bit_extender_4_out), .\dist (4'b1011), .out(shifter_5_out));
  or or_1 (Exponent_out_of_range, subtractor_2_bout, adder_1_cout);
  Adder #(.width(12)) adder_4 (.a(shifter_3_out), .b(shifter_5_out), .out(adder_4_out), .cin(and_2_out));  // open: cout

  // Notes on the sheet:
  //   the ckt shifts right once if carry = 1, then gives that as output
  //   add 1 to exponent if carry = 1
  //   LSB
  //   adds LSB only if right shift happens
  //   adding carry to msb
  //   rounding
  //   amount by which fraction is left shifted
endmodule

module big_ALU (
  input  [11:0] A,
  input  [11:0] B,
  input  sign_A,
  input  sign_B,
  output [11:0] \output ,
  output carry_out,
  output sign_bit_output
);

  wire adder_1_cout, comparator_1_gt, multiplexer_1_out, subtractor_1_bout, xor_1_out;
  wire [11:0] adder_1_out, multiplexer_2_out, negator_1_out, subtractor_1_out;

  xor xor_1 (xor_1_out, sign_A, sign_B);
  Adder #(.width(12)) adder_1 (.a(A), .b(B), .out(adder_1_out), .cout(adder_1_cout));  // open: cin
  Subtractor #(.width(12)) subtractor_1 (.a(A), .b(B), .out(subtractor_1_out), .bout(subtractor_1_bout));  // open: bin
  Comparator #(.width(12), .mode("unsigned")) comparator_1 (.a(A), .b(B), .gt(comparator_1_gt));  // open: eq, lt
  Negator #(.width(12)) negator_1 (.in(subtractor_1_out), .out(negator_1_out));
  Multiplexer #(.enable("false")) multiplexer_1 (
    .in0(sign_B), .in1(sign_A), .out(multiplexer_1_out), .sel(comparator_1_gt));
  Multiplexer #(.width(12), .enable("false")) multiplexer_2 (
    .in0(subtractor_1_out), .in1(negator_1_out), .out(multiplexer_2_out), .sel(subtractor_1_bout));
  Multiplexer #(.enable("false")) multiplexer_3 (.in0(adder_1_cout), .in1(1'b0), .out(carry_out), .sel(xor_1_out));
  Multiplexer #(.width(12), .enable("false")) multiplexer_4 (
    .in0(adder_1_out), .in1(multiplexer_2_out), .out(\output ), .sel(xor_1_out));
  Multiplexer #(.enable("false")) multiplexer_5 (
    .in0(sign_B), .in1(multiplexer_1_out), .out(sign_bit_output), .sel(xor_1_out));

  // Notes on the sheet:
  //   A>B?
  //   used to go to mux to carry in bit 0
  //   sum
  //   absolute difference
  //   IF signs same, return B's sign, else return greater val's sign
endmodule
